# Fritzing sketch cronografo (saved by Fritzing 0.9.2b)
breadboards: 1

parts:
  Parte1 = Arduino Uno (Rev3)
  Parte2 = DeuLigne 1.1 - The Snootlab's LCD shield for Arduino  # not connected
  LED_IR = LED - 3mm [color="Red (633nm)" package="3 mm [THT]"]
  LED_IR_2 = LED - 3mm [color="Red (633nm)" package="3 mm [THT]"]
  sensor_1 = LED - 3mm [color="Red (633nm)" package="3 mm [THT]"]
  sensor_2 = LED - 3mm [color="Red (633nm)" package="3 mm [THT]"]
  R1 = Resistor [tolerance=±5% resistance=330 package=THT]
  R2 = Resistor [tolerance=±5% resistance=330 package=THT]
  R3 = Resistor [tolerance=±5% resistance=82k package=THT]
  R4 = Resistor [tolerance=±5% resistance=82k package=THT]

nets:
  N1: Parte1.D2, sensor_1.cathode, R4.Pin_1
  N2: Parte1.D3_PWM, sensor_2.cathode, R3.Pin_1
  N3: Parte1.5V, R1.Pin_0, R2.Pin_0, R3.Pin_0, R4.Pin_0
  N4: Parte1.GND, LED_IR.cathode, LED_IR_2.cathode, sensor_1.anode, sensor_2.anode
  N5: LED_IR.anode, R1.Pin_1
  N6: LED_IR_2.anode, R2.Pin_1

notes:
  el panel LCD es un shield, se conecta directamente sobre el arduino, y los cables irian sobre los pines del LCD
  fotodiodo Sfh 203 Fa
  led IR de 850 o 900 nm
